# Fritzing sketch plant_buddy_v2_MKR_1310 (saved by Fritzing 0.9.9b)
breadboards: 1

parts:
  RHT1 = Humidity and Temperature Sensor RHT03
  Chirp!_Soil_Moisture_Sensor1 = Chirp! Soil Moisture Sensor v2.7.3
  DS1 = DS18B20 1-Wire Temperature Sensor [part_number=DS18B20]
  R1 = Resistor [tolerance=±5% resistance=4.7 package="0402 [SMD]"]
  Part3 = Arduino MKR WAN 1310
  Part2 = Ambient Light Sensor (TEMT6000 Breakout Board)

nets:
  VCC: RHT1.Vcc, Chirp!_Soil_Moisture_Sensor1.Pin_1, DS1.VDD, R1.Pin_1, Part2.VCC
  N1: RHT1.Data-signal, Part3.D2
  GND: RHT1.GND_1, Chirp!_Soil_Moisture_Sensor1.pin_5, DS1.GND, Part2.GND
  N2: Chirp!_Soil_Moisture_Sensor1.pin_3, Part3.A0
  N3: DS1.DQ, R1.Pin_0, Part3.D3~
  N4: Part3.RESET, Part3.D14/TX
  N5: Part3.D11/MOSI, Part3.+5V
  N6: Part3.A4, Part2.S

custom parts:
  Arduino MKR WAN 1310: The Arduino MKR WAN 1310 board provides a practical and cost effective solution to add LoRa® connectivity to projects requiring low power. This open source board can be connected to: the Arduino IoT Cloud, your own LoRa® network using the Arduino LoRa® PRO Gateway, existing LoRaWAN™ infrastructure like The Things Network, or even other boards using the direct connectivity mode.
